# Fritzing sketch relay_basic (saved by Fritzing 0.9.3b)
breadboards: 1

parts:
  A1 = ESP32 DevKitc V4
  KY-1 = Keyes Relay [package=THT]
  S1 = Pushbutton [package="[THT]"]
  LED1 = LEDs [package=led10mm]
  Clavija = Lilypad Battery Connect
  R1 = Resistor [tolerance=±5% resistance=1k package=THT]

nets:
  N1: A1.Pin_1, S1.Pin_1, S1.Pin_2
  N2: A1.Pin_5, S1.Pin_3, S1.Pin_4, R1.Pin_1
  N3: A1.Pin_9, KY-1.signal
  N4: A1.Pin_14, A1.Pin_32, A1.Pin_38
  N5: A1.Pin_19, KY-1.power
  N6: KY-1.ground, R1.Pin_0
  N7: KY-1.NC, Clavija.-
  N8: KY-1.C, LED1.C
  N9: LED1.A, Clavija.+

custom parts:
  ESP32 DevKitc V4: ESP32-DevKitC board with ESP32-WROOM-32 module. ESP32-DevKitC V4 is a small-sized ESP32-based development board produced by Espressif. Most of the pins on the ESP module are broken out to the pin headers on the board. The pins D0, D1, D2, D3, CMD and CLK are used internally for communication between ESP32 and SPI flash memory. They are grouped on both sides near the USB connector. Avoid using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
  Keyes Relay: The Keyes 5V relay module is suitable for SCM development, home appliance control. It uses a 5V~12V TIL control signal which can control DC / AC signal.
  LEDs: LEDs Standard schematic elements and footprints for 5mm, 3mm, 1206, and 0603 sized LEDs. 5mm - Spark Fun Electronics SKU : COM-00529 (and others)
